# Fritzing sketch fritzingSchema (saved by Fritzing 0.9.3b)
breadboards: 1

parts:
  U1 = NodeMCU V1.0
  R1 = Resistor [tolerance=±20% resistance=10k package=THT]
  R2 = Photocell (LDR) [package=THT]
  Driver1 = 28BYJ-48 Driver Module [part_number=ULN2003 package=THT]
  SM1 = 28BYJ-48 Stepper Motor [part_number=28BYJ-48]

nets:
  N1: U1.3V3, R2.pin_1
  GND: U1.GND, R1.Pin_0, Driver1.GND
  N2: U1.D5, Driver1.IN4
  N3: U1.D6, Driver1.IN3
  N4: U1.D7, Driver1.IN2
  N5: U1.D8, Driver1.IN1
  N6: U1.Vin, Driver1.Vmotor
  N7: U1.A0, R1.Pin_1, R2.pin_0
  N8: Driver1.blue-pin, SM1.blue-pin
  N9: Driver1.pink-pin, SM1.pink-pin
  N10: Driver1.yellow-pin, SM1.yellow-pin
  N11: Driver1.orange-pin, SM1.orange-pin
  N12: Driver1.red-pin, SM1.red-pin

custom parts:
  NodeMCU V1.0: ESP8266 based NodeMCU
  28BYJ-48 Driver Module: ULN2003 Driver Module for the 28BYJ-48 Unipolar Stepper Motor LED A - Blue wire - Bottom coil left LED B - Pink wire - Top coil left LED C - Yellow wire - Bottom coil right LED D - Orange wire - Top coil right Common rail - red Connector pins: blue - pink - yellow - orange - red Control pins - IN1 to IN4 Power pins - GND & Vmotor (5-12V) On/Off jumper (if removed, power to motor is cut).
  28BYJ-48 Stepper Motor: Unipolar Stepper Motor 28BYJ-48 Top coil - pink & orange Bottom coil - blue & yellow Common rail - red Connector pins: blue - pink - yellow - orange - red
